// Logisim project Porte.circ as structural Verilog: 2 circuits, main circuit main
module main (
  input  [31:0] Input,
  output Fail
);

  wire clock_1_out, multiplexer_1_out, multiplexer_2_out;
  wire [4:0] counter_1_q;
  wire [31:0] rom_1_data;

  Counter #(.width(5), .max('h1f)) counter_1 (.Q(counter_1_q), .clk(clock_1_out));  // open: load, D, count, carry, clr
  Clock clock_1 (.out(clock_1_out));
  Multiplexer #(.select(5)) multiplexer_1 (
    .in0(Input[31]), .in1(Input[30]), .in2(Input[29]), .in3(Input[28]), .in4(Input[27]), .in5(Input[26]),
    .in6(Input[25]), .in7(Input[24]), .in8(Input[23]), .in9(Input[22]), .in10(Input[21]), .in11(Input[20]),
    .in12(Input[19]), .in13(Input[18]), .in14(Input[17]), .in15(Input[16]), .in16(Input[15]),
    .in17(Input[14]), .in18(Input[13]), .in19(Input[12]), .in20(Input[11]), .in21(Input[10]),
    .in22(Input[9]), .in23(Input[8]), .in24(Input[7]), .in25(Input[6]), .in26(Input[5]), .in27(Input[4]),
    .in28(Input[3]), .in29(Input[2]), .in30(Input[1]), .in31(Input[0]), .out(multiplexer_1_out),
    .sel(counter_1_q));  // open: en
  Black_Box black_box_1 (.in_1(multiplexer_1_out), .in_2(multiplexer_2_out), .out_3(Fail));
  Multiplexer #(.select(5)) multiplexer_2 (
    .in0(rom_1_data[31]), .in1(rom_1_data[30]), .in2(rom_1_data[29]), .in3(rom_1_data[28]),
    .in4(rom_1_data[27]), .in5(rom_1_data[26]), .in6(rom_1_data[25]), .in7(rom_1_data[24]),
    .in8(rom_1_data[23]), .in9(rom_1_data[22]), .in10(rom_1_data[21]), .in11(rom_1_data[20]),
    .in12(rom_1_data[19]), .in13(rom_1_data[18]), .in14(rom_1_data[17]), .in15(rom_1_data[16]),
    .in16(rom_1_data[15]), .in17(rom_1_data[14]), .in18(rom_1_data[13]), .in19(rom_1_data[12]),
    .in20(rom_1_data[11]), .in21(rom_1_data[10]), .in22(rom_1_data[9]), .in23(rom_1_data[8]),
    .in24(rom_1_data[7]), .in25(rom_1_data[6]), .in26(rom_1_data[5]), .in27(rom_1_data[4]),
    .in28(rom_1_data[3]), .in29(rom_1_data[2]), .in30(rom_1_data[1]), .in31(rom_1_data[0]),
    .out(multiplexer_2_out), .sel(counter_1_q));  // open: en
  ROM #(.addrWidth(2), .dataWidth(32)) rom_1 (.addr(2'b00), .data(rom_1_data));  // open: sel

  // Notes on the sheet:
  //   contents of rom_1 (hex, n*v repeats v):
  //   b4c5d38a
endmodule

module Black_Box (
  input  in_1,
  input  in_2,
  output out_3
);

  wire and_1_out, and_2_out, not_1_out, not_2_out;

  not not_1 (not_1_out, in_1);
  and and_1 (and_1_out, ~not_1_out, in_2);  // AND_Gate
  and and_2 (and_2_out, ~in_1, not_2_out);  // AND_Gate
  not not_2 (not_2_out, in_2);
  or or_1 (out_3, and_1_out, and_2_out);
endmodule
